// Logisim project dot86.circ as structural Verilog: 5 circuits, main circuit cpu
module cpu (
);

  wire and_1_out, and_2_out, buffer_1_out, buffer_2_out, buffer_3_out, CLK_out, CTRL_UNIT_alu,
       CTRL_UNIT_imm8, CTRL_UNIT_imm32, CTRL_UNIT_m32, CTRL_UNIT_mem_read, CTRL_UNIT_reg_write, CTRL_UNIT_rm,
       CTRL_UNIT_rr, nor_1_out, not_1_out, not_2_out, or_1_out, RESET_out, xor_1_out;
  wire [2:0] CTRL_UNIT_alu_fun, CTRL_UNIT_left_reg, CTRL_UNIT_right_reg;
  wire [7:0] INS_MEM_imm8, INS_MEM_modrm, INS_MEM_op;
  wire [15:0] CTRL_UNIT_pc_out, multiplexer_1_out, PC_q;
  wire [31:0] bit_extender_1_out, demultiplexer_1_out0, demultiplexer_1_out1, demultiplexer_2_out0,
       demultiplexer_2_out1, demultiplexer_3_out0, demultiplexer_3_out1, demultiplexer_6_out1,
       demultiplexer_7_out1, INS_MEM_imm32, REG_FILE_left_out, undriven, undriven_2;

  Button RESET (.out(RESET_out));
  buf buffer_1 (buffer_1_out, RESET_out);
  Clock CLK (.out(CLK_out));
  or or_1 (or_1_out, RESET_out, buffer_3_out);
  buf buffer_2 (buffer_2_out, buffer_1_out);
  buf buffer_3 (buffer_3_out, buffer_2_out);
  Multiplexer #(.width(16)) multiplexer_1 (
    .in0(CTRL_UNIT_pc_out), .in1(16'h400), .out(multiplexer_1_out), .sel(or_1_out));
  Register #(.width(16)) PC (.D(multiplexer_1_out), .en(1'b1), .clk(xor_1_out), .Q(PC_q));  // open: clr
  xor xor_1 (xor_1_out, buffer_3_out, CLK_out);
  instruction_memory INS_MEM (
    .ADDR(PC_q), .CLK(xor_1_out), .OP(INS_MEM_op), .MODRM(INS_MEM_modrm), .IMM8(INS_MEM_imm8),
    .IMM32(INS_MEM_imm32));  // open: DATA, WRT, DISP8, DISP32
  control_unit CTRL_UNIT (
    .OP(INS_MEM_op), .MODRM(INS_MEM_modrm), .PC(PC_q), .ALU_FUN(CTRL_UNIT_alu_fun), .ALU(CTRL_UNIT_alu),
    .REG_WRITE(CTRL_UNIT_reg_write), .MEM_READ(CTRL_UNIT_mem_read), .LEFT_REG(CTRL_UNIT_left_reg),
    .RIGHT_REG(CTRL_UNIT_right_reg), .RR(CTRL_UNIT_rr), .IMM8(CTRL_UNIT_imm8), .IMM32(CTRL_UNIT_imm32),
    .M32(CTRL_UNIT_m32), .RM(CTRL_UNIT_rm), .PC_OUT(CTRL_UNIT_pc_out));  // open: MEM_WRITE, DISP8, DISP32, BRANCH, JUMP
  assign bit_extender_1_out = {{24{1'b0}}, INS_MEM_imm8};  // Bit_Extender bit_extender_1
  and and_1 (and_1_out, ~CTRL_UNIT_mem_read, CTRL_UNIT_alu);  // AND_Gate
  Demultiplexer #(.width(32)) demultiplexer_1 (
    .out0(demultiplexer_1_out0), .out1(demultiplexer_1_out1), .in(demultiplexer_2_out0), .sel(not_1_out));
  Demultiplexer #(.width(32)) demultiplexer_2 (
    .out0(demultiplexer_2_out0), .out1(demultiplexer_2_out1), .in(undriven), .sel(and_1_out));
  nor nor_1 (nor_1_out, CTRL_UNIT_m32, CTRL_UNIT_rm);
  Demultiplexer #(.width(32)) demultiplexer_3 (
    .out0(demultiplexer_3_out0), .out1(demultiplexer_3_out1), .in(demultiplexer_1_out0), .sel(nor_1_out));
  not not_1 (not_1_out, CTRL_UNIT_rr);
  register_file REG_FILE (
    .DATA(undriven), .WRT(CTRL_UNIT_reg_write), .LEFT_REG(CTRL_UNIT_left_reg),
    .RIGHT_REG(CTRL_UNIT_right_reg), .RESET(or_1_out), .CLK(xor_1_out), .LEFT_OUT(REG_FILE_left_out),
    .RIGHT_OUT(demultiplexer_1_out1));
  and and_2 (and_2_out, CTRL_UNIT_imm8, ~CTRL_UNIT_imm32);  // AND_Gate
  Demultiplexer #(.width(32)) demultiplexer_4 (
    .out0(INS_MEM_imm32), .out1(bit_extender_1_out), .in(demultiplexer_3_out1), .sel(and_2_out));
  Demultiplexer #(.width(32)) demultiplexer_5 (
    .out0(INS_MEM_imm32), .out1(bit_extender_1_out), .in(demultiplexer_6_out1), .sel(and_2_out));
  Demultiplexer #(.width(32)) demultiplexer_6 (
    .out0(demultiplexer_3_out0), .out1(demultiplexer_6_out1), .in(demultiplexer_7_out1), .sel(nor_1_out));
  not not_2 (not_2_out, CTRL_UNIT_rr);
  Demultiplexer #(.width(32)) demultiplexer_7 (
    .out0(demultiplexer_1_out1), .out1(demultiplexer_7_out1), .in(undriven_2), .sel(not_2_out));
  arithmetic_logic_unit ALU (
    .L_OPERAND(REG_FILE_left_out), .R_OPERAND(undriven_2), .RESULT(demultiplexer_2_out1));  // open: ZERO, NEGATIVE, CARRY, OVERFLOW
  // also tied to GND on the sheet: {demultiplexer_3_out0[0], demultiplexer_3_out0[1], demultiplexer_3_out0[2], demultiplexer_3_out0[3], demultiplexer_3_out0[4], demultiplexer_3_out0[5], demultiplexer_3_out0[6], demultiplexer_3_out0[7], demultiplexer_3_out0[8], demultiplexer_3_out0[9], demultiplexer_3_out0[10], demultiplexer_3_out0[11], demultiplexer_3_out0[12], demultiplexer_3_out0[13], demultiplexer_3_out0[14], demultiplexer_3_out0[15], demultiplexer_3_out0[16], demultiplexer_3_out0[17], demultiplexer_3_out0[18], demultiplexer_3_out0[19], demultiplexer_3_out0[20], demultiplexer_3_out0[21], demultiplexer_3_out0[22], demultiplexer_3_out0[23], demultiplexer_3_out0[24], demultiplexer_3_out0[25], demultiplexer_3_out0[26], demultiplexer_3_out0[27], demultiplexer_3_out0[28], demultiplexer_3_out0[29], demultiplexer_3_out0[30], demultiplexer_3_out0[31]}

  // Notes on the sheet:
  //   use alu output?
endmodule

module instruction_memory (
  input  [15:0] ADDR,
  input  [47:0] DATA,
  input  WRT,
  input  CLK,
  output [7:0] OP,
  output [7:0] MODRM,
  output [7:0] IMM8,
  output [31:0] IMM32,
  output [7:0] DISP8,
  output [31:0] DISP32
);

  RAM #(.addrWidth(16), .dataWidth(48), .enables("line")) INS_MEM (
    .addr(ADDR), .we(WRT), .clk(CLK), .din(DATA), .dout({DISP32[31:8], DISP8, IMM8, OP}));

  assign DISP32[7:0] = DISP8;
  assign IMM32 = {DISP8, DISP8, DISP8, IMM8};
  assign MODRM = IMM8;
endmodule

module register_file (
  input  [31:0] DATA,
  input  WRT,
  input  [2:0] LEFT_REG,
  input  [2:0] RIGHT_REG,
  input  RESET,
  input  CLK,
  output [31:0] LEFT_OUT,
  output [31:0] RIGHT_OUT
);

  wire undriven, undriven_2, undriven_3, undriven_4, undriven_5, undriven_6, undriven_7, undriven_8;
  wire [31:0] BP_q, DI_q, RA_q, RB_q, RC_q, RD_q, SI_q, SP_q;

  Multiplexer #(.select(3)) multiplexer_1 (
    .in0(undriven), .in1(undriven_2), .in2(undriven_3), .in3(undriven_4), .in4(undriven_5), .in5(undriven_6),
    .in6(undriven_7), .in7(undriven_8), .out(WRT), .sel(LEFT_REG));
  Register #(.width(32)) RA (.D(DATA), .en(undriven), .clk(CLK), .Q(RA_q), .clr(RESET));
  Register #(.width(32)) RB (.D(DATA), .en(undriven_2), .clk(CLK), .Q(RB_q), .clr(RESET));
  Register #(.width(32)) RC (.D(DATA), .en(undriven_3), .clk(CLK), .Q(RC_q), .clr(RESET));
  Register #(.width(32)) RD (.D(DATA), .en(undriven_4), .clk(CLK), .Q(RD_q), .clr(RESET));
  Register #(.width(32)) SP (.D(DATA), .en(undriven_5), .clk(CLK), .Q(SP_q), .clr(RESET));
  Register #(.width(32)) BP (.D(DATA), .en(undriven_6), .clk(CLK), .Q(BP_q), .clr(RESET));
  Register #(.width(32)) SI (.D(DATA), .en(undriven_7), .clk(CLK), .Q(SI_q), .clr(RESET));
  Register #(.width(32)) DI (.D(DATA), .en(undriven_8), .clk(CLK), .Q(DI_q), .clr(RESET));
  Demultiplexer #(.select(3), .width(32)) demultiplexer_1 (
    .out0(RA_q), .out1(RB_q), .out2(RC_q), .out3(RD_q), .out4(SP_q), .out5(BP_q), .out6(SI_q), .out7(DI_q),
    .in(LEFT_OUT), .sel(LEFT_REG));
  Demultiplexer #(.select(3), .width(32)) demultiplexer_2 (
    .out0(RA_q), .out1(RB_q), .out2(RC_q), .out3(RD_q), .out4(SP_q), .out5(BP_q), .out6(SI_q), .out7(DI_q),
    .in(RIGHT_OUT), .sel(RIGHT_REG));
endmodule

module control_unit (
  input  [7:0] OP,
  input  [7:0] MODRM,
  input  [15:0] PC,
  output [2:0] ALU_FUN,
  output ALU,
  output REG_WRITE,
  output MEM_READ,
  output MEM_WRITE,
  output [2:0] LEFT_REG,
  output [2:0] RIGHT_REG,
  output RR,
  output IMM8,
  output IMM32,
  output M32,
  output RM,
  output DISP8,
  output DISP32,
  output [15:0] PC_OUT,
  output BRANCH,
  output JUMP
);

  wire ADD_out, and_1_out, and_2_out, and_3_out, and_4_out, and_5_out, and_6_out, and_7_out, and_8_out,
       and_9_out, and_10_out, disp_out, nand_1_out, or_1_out, or_2_out, or_4_out, or_5_out, or_7_out,
       xor_1_out;
  wire [2:0] multiplexer_2_out;
  wire [15:0] adder_1_out, adder_2_out, multiplexer_1_out, multiplexer_3_out, multiplexer_6_out;

  Multiplexer #(.width(16)) multiplexer_1 (.in0(16'h1), .in1(16'h2), .out(multiplexer_1_out), .sel(or_1_out));
  Adder #(.width(16)) adder_1 (.a(PC), .b(multiplexer_1_out), .out(adder_1_out), .cin(1'b0));  // open: cout
  nand nand_1 (nand_1_out, 1'b1, 1'b1);
  and and_1 (and_1_out, 1'b1, 1'b1);
  buf or_1 (or_1_out, ~and_4_out);  // OR_Gate OR_Gate
  and ADD (ADD_out, ~1'b0, ~1'b0, ~1'b0, ~1'b0, ~1'b0, ~1'b0);  // AND_Gate
  and and_2 (and_2_out, 1'b1, ~and_1_out);  // AND_Gate
  and and_3 (and_3_out, 1'b1, ~and_1_out);  // AND_Gate
  and and_4 (and_4_out, 1'b1, ADD_out);
  buf or_2 (or_2_out, and_4_out);  // OR_Gate
  Multiplexer #(.width(3)) multiplexer_2 (.in0(3'b111), .in1(3'b000), .out(multiplexer_2_out), .sel(or_2_out));
  xor xor_1 (xor_1_out, and_2_out, and_3_out);
  and and_5 (and_5_out, 1'b1, ~1'b1, 1'b1, nand_1_out);  // AND_Gate
  and and_6 (and_6_out, xor_1_out, and_3_out);
  and and_7 (and_7_out, 1'b0, and_4_out, ADD_out);
  buf or_3 (IMM32, and_7_out);  // OR_Gate
  and and_8 (and_8_out, 1'b0, ~1'b1, ADD_out);  // AND_Gate
  buf or_4 (or_4_out, and_8_out);  // OR_Gate
  or or_5 (or_5_out, and_5_out, IMM32, and_6_out);
  Multiplexer #(.width(16)) multiplexer_3 (.in0({16{1'b0}}), .in1(16'h4), .out(multiplexer_3_out), .sel(or_5_out));
  and and_9 (and_9_out, ~and_5_out, or_1_out, ~and_6_out, ~and_1_out);  // AND_Gate
  and and_10 (and_10_out, ~1'b0, and_4_out, ADD_out);  // AND_Gate
  Multiplexer #(.width(3)) multiplexer_4 (.in0(multiplexer_2_out), .in1(3'b111), .out(LEFT_REG), .sel(or_4_out));
  Multiplexer #(.width(3)) multiplexer_5 (.in0(3'b111), .in1(multiplexer_2_out), .out(RIGHT_REG), .sel(or_4_out));
  or disp (disp_out, and_3_out, and_2_out);
  Adder #(.width(16)) adder_2 (.a(adder_1_out), .b(multiplexer_3_out), .out(adder_2_out), .cin(1'b0));  // open: cout
  buf or_6 (IMM8, and_10_out);  // OR_Gate
  Multiplexer #(.width(16)) multiplexer_6 (.in0({16{1'b0}}), .in1(16'h1), .out(multiplexer_6_out), .sel(or_7_out));
  or or_7 (or_7_out, IMM8, and_9_out);
  and and_11 (RR, or_1_out, and_1_out);
  and and_12 (M32, and_5_out, ~disp_out, or_1_out);  // AND_Gate
  and and_13 (RM, ~and_5_out, ~disp_out, ~and_1_out, or_1_out);  // AND_Gate
  and and_14 (DISP8, ~and_6_out, disp_out, or_1_out);  // AND_Gate
  and and_15 (DISP32, and_6_out, disp_out, or_1_out);
  Adder #(.width(16)) adder_3 (.a(adder_2_out), .b(multiplexer_6_out), .out(PC_OUT), .cin(1'b0));  // open: cout
  Priority_Encoder priority_encoder_1 (
    .in0(ADD_out), .out(ALU_FUN), .en_in(1'b1), .gs(ALU));  // open: in1, in2, in3, in4, in5, in6, in7, en_out
  buf or_8 (REG_WRITE, ADD_out);  // OR_Gate

  assign BRANCH = 1'b0;
  assign JUMP = 1'b0;
  assign MEM_READ = 1'b0;
  assign MEM_WRITE = 1'b0;

  // Notes on the sheet:
  //   modrm?
  //   use RA reg?
  //   imm32?
  //   flip regs?
  //   imm8?
endmodule

module arithmetic_logic_unit (
  input  [31:0] L_OPERAND,
  input  [31:0] R_OPERAND,
  output [31:0] RESULT,
  output ZERO,
  output NEGATIVE,
  output CARRY,
  output OVERFLOW
);

  Adder #(.width(32)) adder_1 (.a(L_OPERAND), .b(R_OPERAND));  // open: out, cin, cout
  Adder #(.width(16)) adder_2 ();  // open: a, b, out, cin, cout
  Multiplier multiplier_1 ();  // open: a, b, out, cin, cout
  Divider divider_1 ();  // open: a, b, out, upper, rem
  Subtractor subtractor_1 ();  // open: a, b, out, bin, bout
endmodule
